# Fritzing sketch Esquema Circuito (saved by Fritzing 0.9.3b)
breadboards: 1

parts:
  IR1 = TSOP312.., 314.. [package=THT]
  LED1 = LED - 5mm [color="Red (633nm)" package="5 mm [THT]"]
  Componente1 = Arduino Pro Mini v13
  U1 = ESP8266 WiFi Module [part_number=ESP8266]
  R1 = Resistor [tolerance=±5% resistance=220 package="0402 [SMD]"]
  R3 = Resistor [tolerance=±5% resistance=20k package="2010 [SMD]"]
  R4 = Resistor [tolerance=±5% resistance=20k package="0603 [SMD]"]
  R5 = Resistor [tolerance=±5% resistance=20k package="2010 [SMD]"]
  R6 = Resistor [tolerance=±5% resistance=10k package="2010 [SMD]"]
  R8 = Resistor [tolerance=±5% resistance=20k package="2010 [SMD]"]
  R7 = Resistor [tolerance=±5% resistance=10k package="2010 [SMD]"]

nets:
  N1: IR1.GND, Componente1.D3_PWM
  N2: IR1.Vs, LED1.cathode, R1.Pin_1
  N3: IR1.Data, Componente1.VCC, R3.Pin_1
  GND: LED1.anode, Componente1.GND, U1.GND, R1.Pin_0, R4.Pin_0, R5.Pin_1, R8.Pin_1
  N4: Componente1.D0/TX, R7.Pin_0
  N5: Componente1.D1/RX, R6.Pin_0
  N6: U1.TX, R5.Pin_0, R6.Pin_1
  N7: U1.RX, R8.Pin_0, R7.Pin_1
  N8: U1.3.3V, R3.Pin_0, R4.Pin_1
