# Fritzing sketch Esquema Circuito (saved by Fritzing 0.9.3b)
breadboards: 2

parts:
  IR1 = TSOP312.., 314.. [package=THT]
  LED1 = LED - 5mm [color="Red (633nm)" package="5 mm [THT]"]
  R3 = Resistor [tolerance=±5% resistance=20k package="2010 [SMD]"]
  R4 = Resistor [tolerance=±5% resistance=20k package="0603 [SMD]"]
  R5 = Resistor [tolerance=±5% resistance=20k package="2010 [SMD]"]
  R6 = Resistor [tolerance=±5% resistance=10k package="2010 [SMD]"]
  R8 = Resistor [tolerance=±5% resistance=20k package="2010 [SMD]"]
  R7 = Resistor [tolerance=±5% resistance=10k package="2010 [SMD]"]
  U2 = ESP8266 WiFi Module [part_number=ESP8266]
  Pro_Micro1 = SparkFun Pro Micro
  J1 = Infrared Proximity Sensor
  IR2 = TSOP312.., 314.. [package=THT]
  J2 = Infrared Proximity Sensor
  LED2 = LED - 5mm [color="Red (633nm)" package="5 mm [THT]"]
  U5 = NodeMCU V3.0

nets:
  N1: IR1.GND, U2.GPIO_2
  GND: IR1.Vs, LED1.cathode, R4.Pin_0, R5.Pin_1, R8.Pin_1, U2.GND, Pro_Micro1.GND, J1.GND
  VCC: IR1.Data, LED1.anode, R3.Pin_0, R4.Pin_1, U2.VCC, U2.CH_PD, J1.Vcc
  N2: R3.Pin_1, Pro_Micro1.VCC
  N3: R5.Pin_0, R6.Pin_1, U2.TXD
  N4: R6.Pin_0, Pro_Micro1.RX1, Pro_Micro1.8
  N5: R8.Pin_0, R7.Pin_1, U2.RXD
  N6: R7.Pin_0, Pro_Micro1.TX0
  N7: IR2.GND, U5.D2
  GND_2: IR2.Vs, J2.GND, LED2.cathode, U5.GND
  VCC_2: IR2.Data, J2.Vcc, LED2.anode, U5.3V3
  N8: J2.Vout, U5.D1

notes:
  Sensor de proximidade básico
  Módulo sensor de proximidade
  NodeMCU
  ESP8266 ESP-01
  Arduino pro micro

custom parts:
  ESP8266 WiFi Module: Generic WiFi Module based on the ESP8266 with onboard PCB antenna and UART communications
  SparkFun Pro Micro: The Pro Micro is similar to the Pro Mini except with an ATmega32U4 on board. The USB transceiver inside the 32U4 allows us to add USB connectivity on-board and do away with bulky external USB interface. Based on: https://github.com/unorthodox-engineers/unorthodox-arduino/blob/master/Unorthodox/fritzing/parts/Pro%20Micro.fzpz
  NodeMCU V3.0: ESP8266 based NodeMCU
